// Logisim project lab6.circ as structural Verilog: 2 circuits, main circuit main
module main (
  input  i_0,
  input  i_1,
  input  i_2,
  input  i_3,
  input  i_4,
  input  i_5,
  input  i_6,
  input  i_7,
  input  i_8,
  input  SHR,
  input  SHL,
  output O8,
  output O7,
  output O6,
  output O5,
  output O4,
  output O3,
  output O2,
  output O1,
  output O0
);

  wire and_1_out, and_2_out, and_3_out, and_4_out, and_5_out, and_6_out, and_7_out, and_8_out, and_9_out,
       and_10_out, and_11_out, and_12_out, and_13_out, and_14_out, and_15_out, and_16_out, and_17_out,
       and_18_out, and_19_out, and_20_out, and_21_out, and_22_out, and_23_out, and_24_out, and_25_out,
       and_26_out, and_27_out, not_1_out, not_2_out, not_3_out, not_4_out, not_5_out, not_6_out, not_7_out,
       not_8_out, not_9_out, not_10_out, not_11_out, not_12_out, not_13_out, not_14_out, not_15_out,
       not_16_out, not_17_out, not_18_out;

  and and_1 (and_1_out, SHR, i_0);
  not not_1 (not_1_out, SHL);
  not not_2 (not_2_out, SHR);
  and and_2 (and_2_out, not_1_out, i_8, not_2_out);
  or or_1 (O8, and_1_out, and_2_out, and_3_out);
  and and_3 (and_3_out, SHL, i_7);
  not not_3 (not_3_out, SHL);
  and and_4 (and_4_out, SHR, i_8);
  not not_4 (not_4_out, SHR);
  and and_5 (and_5_out, not_3_out, i_7, not_4_out);
  and and_6 (and_6_out, SHL, i_6);
  or or_2 (O7, and_4_out, and_5_out, and_6_out);
  not not_5 (not_5_out, SHR);
  and and_7 (and_7_out, SHR, i_7);
  and and_8 (and_8_out, not_5_out, i_6, not_6_out);
  or or_3 (O6, and_7_out, and_8_out, and_9_out);
  not not_6 (not_6_out, SHL);
  and and_9 (and_9_out, SHL, i_5);
  and and_10 (and_10_out, SHR, i_6);
  not not_7 (not_7_out, SHR);
  not not_8 (not_8_out, SHL);
  and and_11 (and_11_out, not_7_out, i_5, not_8_out);
  or or_4 (O5, and_10_out, and_11_out, and_12_out);
  and and_12 (and_12_out, SHL, i_4);
  not not_9 (not_9_out, SHL);
  and and_13 (and_13_out, SHR, i_5);
  not not_10 (not_10_out, SHR);
  and and_14 (and_14_out, SHL, i_3);
  and and_15 (and_15_out, not_9_out, i_4, not_10_out);
  or or_5 (O4, and_13_out, and_15_out, and_14_out);
  not not_11 (not_11_out, SHL);
  and and_16 (and_16_out, SHR, i_4);
  and and_17 (and_17_out, not_11_out, i_3, not_12_out);
  or or_6 (O3, and_16_out, and_17_out, and_18_out);
  not not_12 (not_12_out, SHR);
  and and_18 (and_18_out, SHL, i_2);
  and and_19 (and_19_out, SHR, i_3);
  not not_13 (not_13_out, SHR);
  not not_14 (not_14_out, SHL);
  and and_20 (and_20_out, not_13_out, i_2, not_14_out);
  or or_7 (O2, and_19_out, and_20_out, and_21_out);
  and and_21 (and_21_out, SHL, i_1);
  not not_15 (not_15_out, SHR);
  and and_22 (and_22_out, SHR, i_2);
  and and_23 (and_23_out, not_15_out, i_1, not_16_out);
  or or_8 (O1, and_22_out, and_23_out, and_24_out);
  not not_16 (not_16_out, SHL);
  and and_24 (and_24_out, SHL, i_0);
  and and_25 (and_25_out, SHR, i_1);
  not not_17 (not_17_out, SHR);
  not not_18 (not_18_out, SHL);
  and and_26 (and_26_out, not_17_out, i_0, not_18_out);
  or or_9 (O0, and_25_out, and_26_out, and_27_out);
  and and_27 (and_27_out, SHL, i_8);
endmodule

module teste (
  input  in_1,
  input  in_2
);

  wire clk, O0, O1, O2, O3, O4, O5, O6, O7, O8, Q0, Q1, Q2, Q3, Q4, Q5, Q6, Q7, Q8;

  Clock clock_1 (.out(clk));
  main main_1 (
    .i_0(Q0), .i_1(Q1), .i_2(Q2), .i_3(Q3), .i_4(Q4), .i_5(Q5), .i_6(Q6), .i_7(Q7), .i_8(Q8), .SHR(in_1),
    .SHL(in_2), .O8(O8), .O7(O7), .O6(O6), .O5(O5), .O4(O4), .O3(O3), .O2(O2), .O1(O1), .O0(O0));
  LED led_1 (.in(O0));
  D_Flip_Flop d_ff_1 (.D(O0), .clk(clk), .Q(Q0));  // open: Qn, preset, reset
  D_Flip_Flop d_ff_2 (.D(O1), .clk(clk), .Q(Q1));  // open: Qn, preset, reset
  D_Flip_Flop d_ff_3 (.D(O2), .clk(clk), .Q(Q2));  // open: Qn, preset, reset
  D_Flip_Flop d_ff_4 (.D(O3), .clk(clk), .Q(Q3));  // open: Qn, preset, reset
  D_Flip_Flop d_ff_5 (.D(O4), .clk(clk), .Q(Q4));  // open: Qn, preset, reset
  D_Flip_Flop d_ff_6 (.D(O5), .clk(clk), .Q(Q5));  // open: Qn, preset, reset
  D_Flip_Flop d_ff_7 (.D(O6), .clk(clk), .Q(Q6));  // open: Qn, preset, reset
  D_Flip_Flop d_ff_8 (.D(O7), .clk(clk), .Q(Q7));  // open: Qn, preset, reset
  DotMatrix dotmatrix_1 ();  // open: col0, col1, col2, col3, col4
  D_Flip_Flop d_ff_9 (.D(O8), .clk(clk), .Q(Q8));  // open: Qn, preset, reset
endmodule
